// Logisim project 1-Registrador do tipo D.circ as structural Verilog: 2 circuits, main circuit Flip flop do tipo de D
module Flip_flop_do_tipo_de_D (
  input  C,
  input  D,
  output Q,
  output nQ
);

  wire and_1_out, and_2_out, not_1_out;

  Clock Clock ();  // open: out
  not not_1 (not_1_out, D);
  and and_1 (and_1_out, not_1_out, C);
  and and_2 (and_2_out, C, D);
  nor nor_1 (Q, and_1_out, nQ);
  nor nor_2 (nQ, Q, and_2_out);
endmodule

module Flip_flop_do_tipo_jk (
  input  J,
  input  K,
  input  in_3,
  output Q,
  output nQ
);

  wire nand_1_out, nand_2_out, nand_3_out, not_1_out;

  nand nand_1 (nand_1_out, nQ, J);
  not not_1 (not_1_out, K);
  nand nand_2 (nand_2_out, not_1_out, Q);
  nand nand_3 (nand_3_out, nand_1_out, nand_2_out);
  Flip_flop_do_tipo_de_D flip_flop_do_tipo_de_d_1 (.D(nand_3_out), .Q(Q), .nQ(nQ), .C(in_3));
endmodule
