// Logisim project 11-Extensor de sinal de 4 bits para 8 bits.circ as structural Verilog: 1 circuit, main circuit main
module main (
  input  A3,
  input  A2,
  input  A1,
  input  A0,
  input  Extensor,
  output [7:0] out_6
);

  and and_1 (out_6[4], Extensor, Extensor);
  and and_2 (out_6[5], Extensor, Extensor);
  and and_3 (out_6[6], Extensor, Extensor);
  and and_4 (out_6[7], Extensor, Extensor);

  assign out_6[3:0] = {A3, A2, A1, A0};

  // Notes on the sheet:
  //   A3 será o bit mais significativo
endmodule
