// Logisim project 13-contador_sincrono.circ as structural Verilog: 2 circuits, main circuit main
module main (
  input  in_1,
  input  in_2,
  input  in_3,
  output out_4,
  output out_5,
  output out_6,
  output out_7
);

  wire and_1_out, and_2_out;

  jk jk_1 (.j(and_1_out), .clk(in_1), .k(and_1_out), .c(in_2), .out_6(out_6));  // open: p, out_7
  and and_1 (and_1_out, out_4, and_2_out);
  jk jk_2 (.j(and_2_out), .clk(in_1), .k(and_2_out), .c(in_2), .out_6(out_4));  // open: p, out_7
  and and_2 (and_2_out, out_5, out_7);
  jk jk_3 (.j(out_7), .clk(in_1), .k(out_7), .c(in_2), .out_6(out_5));  // open: p, out_7
  jk jk_4 (.j(in_3), .clk(in_1), .k(in_3), .c(in_2), .out_6(out_7));  // open: p, out_7
endmodule

module jk (
  input  p,
  input  j,
  input  clk,
  input  k,
  input  c,
  output out_6,
  output out_7
);

  wire nand_1_out, nand_2_out, nand_3_out, nand_4_out, nand_5_out, nand_6_out, not_1_out;

  nand nand_1 (nand_1_out, j, clk, out_7);
  nand nand_2 (nand_2_out, out_6, clk, k);
  not not_1 (not_1_out, clk);
  nand nand_3 (nand_3_out, p, nand_1_out, nand_4_out);
  nand nand_4 (nand_4_out, nand_3_out, nand_2_out, c);
  nand nand_5 (nand_5_out, not_1_out, nand_3_out);
  nand nand_6 (nand_6_out, nand_4_out, not_1_out);
  nand nand_7 (out_6, p, nand_5_out, out_7);
  nand nand_8 (out_7, nand_6_out, out_6, c);
endmodule
