// Logisim project 17-detector_primo.circ as structural Verilog: 1 circuit, main circuit detector
module detector (
  input  [3:0] Entrada,
  output \Saída 
);

  wire and_1_out, and_2_out, and_3_out, and_4_out, not_1_out, not_2_out, not_3_out, not_4_out, not_5_out;

  not not_1 (not_1_out, Entrada[3]);
  and and_1 (and_1_out, not_1_out, not_2_out, Entrada[1]);
  not not_2 (not_2_out, Entrada[2]);
  or or_1 (\Saída , and_1_out, and_2_out, and_4_out, and_3_out);
  and and_2 (and_2_out, Entrada[2], not_4_out, Entrada[0]);
  not not_3 (not_3_out, Entrada[2]);
  not not_4 (not_4_out, Entrada[1]);
  and and_3 (and_3_out, not_5_out, Entrada[2], Entrada[0]);
  and and_4 (and_4_out, not_3_out, Entrada[1], Entrada[0]);
  not not_5 (not_5_out, Entrada[3]);

  // Notes on the sheet:
  //   valor 13
endmodule
