// Logisim project 2-multiplexadoe_4entradas.circ as structural Verilog: 1 circuit, main circuit main
module main (
  input  A,
  input  B,
  input  C,
  input  D,
  input  S0,
  input  S1,
  output S
);

  wire and_1_out, and_2_out, and_3_out, and_4_out, not_1_out, not_2_out, not_3_out, not_4_out;

  not not_1 (not_1_out, S0);
  not not_2 (not_2_out, S1);
  not not_3 (not_3_out, S0);
  not not_4 (not_4_out, S1);
  and and_1 (and_1_out, A, not_1_out, not_2_out);
  and and_2 (and_2_out, B, not_3_out, S1);
  and and_3 (and_3_out, C, S0, not_4_out);
  and and_4 (and_4_out, D, S0, S1);
  or or_1 (S, and_1_out, and_2_out, and_3_out, and_4_out);
endmodule
