// Logisim project 1 to 8 Demultiplexer.circ as structural Verilog: 1 circuit, main circuit  1 to 8 Demultiplexer
module _1_to_8_Demultiplexer (
  input  S2,
  input  S1,
  input  S0,
  input  D,
  output Y7,
  output Y6,
  output Y5,
  output Y4,
  output Y3,
  output Y2,
  output Y1,
  output Y0
);

  wire not_1_out, not_2_out, not_3_out;

  not not_1 (not_1_out, S2);
  not not_2 (not_2_out, S1);
  not not_3 (not_3_out, S0);
  and and_1 (Y7, S0, S1, S2, D);
  and and_2 (Y6, S0, S1, S2, D);
  and and_3 (Y5, S0, not_2_out, S2, D);
  and and_4 (Y4, not_3_out, not_2_out, S2, D);
  and and_5 (Y3, S0, S1, not_1_out, D);
  and and_6 (Y2, not_3_out, S1, not_1_out, D);
  and and_7 (Y1, S0, not_2_out, not_1_out, D);
  and and_8 (Y0, not_3_out, not_2_out, not_1_out, D);

  // Notes on the sheet:
  //   S2
  //   S1
  //   S0
  //   D
endmodule
