// Logisim project Multiplexador 8x1 8BITS.circ as structural Verilog
// Mux
module main (
  input  [7:0] in_1,
  input  [7:0] in_2,
  input  S,
  output [7:0] out_4
);

  wire and_1_out, and_2_out, and_3_out, and_4_out, and_5_out, and_6_out, and_7_out, and_8_out, and_9_out,
       and_10_out, and_11_out, and_12_out, and_13_out, and_14_out, and_15_out, and_16_out, not_1_out,
       not_2_out, not_3_out, not_4_out, not_5_out, not_6_out, not_7_out, not_8_out;

  not not_1 (not_1_out, S);
  not not_2 (not_2_out, S);
  not not_3 (not_3_out, S);
  not not_4 (not_4_out, S);
  not not_5 (not_5_out, S);
  and and_1 (and_1_out, in_2[7], S);
  and and_2 (and_2_out, in_1[6], not_1_out);
  and and_3 (and_3_out, in_2[6], S);
  and and_4 (and_4_out, in_1[5], not_2_out);
  and and_5 (and_5_out, in_2[5], S);
  and and_6 (and_6_out, in_1[4], not_3_out);
  and and_7 (and_7_out, in_2[4], S);
  and and_8 (and_8_out, in_1[3], not_4_out);
  and and_9 (and_9_out, in_2[3], S);
  and and_10 (and_10_out, in_1[7], not_5_out);
  or or_1 (out_4[7], and_10_out, and_1_out);
  or or_2 (out_4[6], and_2_out, and_3_out);
  or or_3 (out_4[5], and_4_out, and_5_out);
  or or_4 (out_4[4], and_6_out, and_7_out);
  or or_5 (out_4[3], and_8_out, and_9_out);
  not not_6 (not_6_out, S);
  not not_7 (not_7_out, S);
  not not_8 (not_8_out, S);
  and and_11 (and_11_out, in_1[0], not_6_out);
  and and_12 (and_12_out, in_2[0], S);
  and and_13 (and_13_out, in_1[1], not_7_out);
  and and_14 (and_14_out, in_2[1], S);
  and and_15 (and_15_out, in_1[2], not_8_out);
  and and_16 (and_16_out, in_2[2], S);
  or or_6 (out_4[2], and_11_out, and_12_out);
  or or_7 (out_4[1], and_13_out, and_14_out);
  or or_8 (out_4[0], and_15_out, and_16_out);
endmodule
