// Logisim project Mux 8x1 8bits.circ as structural Verilog: 2 circuits, main circuit main
// Mux
module main (
  input  [7:0] in_1,
  input  [7:0] in_2,
  input  [7:0] in_3,
  input  [7:0] in_4,
  input  [1:0] in_5,
  output [7:0] out_6
);

  wire [7:0] main_1_out_4, main_2_out_4;

  Multiplexador_8x1_8BITS_main main_1 (.in_2(in_4), .in_1(in_3), .out_4(main_1_out_4), .S(in_5[0]));
  Multiplexador_8x1_8BITS_main main_2 (.in_2(in_2), .in_1(in_1), .out_4(main_2_out_4), .S(in_5[0]));
  Multiplexador_8x1_8BITS_main main_3 (.in_2(main_2_out_4), .in_1(main_1_out_4), .out_4(out_6), .S(in_5[1]));
endmodule

module MUX_8X1_8bits (
  input  [7:0] in_1,
  input  [7:0] in_2,
  input  [7:0] in_3,
  input  [7:0] in_4,
  input  [2:0] in_5,
  input  [7:0] in_6,
  input  [7:0] in_7,
  input  [7:0] in_8,
  input  [7:0] in_9,
  output [7:0] out_10
);

  wire [7:0] main_1_out_6, main_2_out_6;

  main main_1 (.in_1(in_1), .in_2(in_2), .in_3(in_3), .in_4(in_4), .in_5(in_5[1:0]), .out_6(main_1_out_6));
  main main_2 (.in_1(in_6), .in_2(in_7), .in_3(in_8), .in_4(in_9), .in_5(in_5[1:0]), .out_6(main_2_out_6));
  Multiplexador_8x1_8BITS_main main_3 (.in_2(main_2_out_6), .in_1(main_1_out_6), .out_4(out_10), .S(in_5[2]));
endmodule
