// Logisim project RAM.circ as structural Verilog: 1 circuit, main circuit main
module main (
  input  [7:0] in_1,
  input  SET,
  input  CLEAR,
  input  [2:0] in_4,
  input  [2:0] in_5,
  output [7:0] out_6
);

  wire clock_1_out, n1_to_8_demultiplexer_1_y0, n1_to_8_demultiplexer_1_y1, n1_to_8_demultiplexer_1_y2,
       n1_to_8_demultiplexer_1_y3, n1_to_8_demultiplexer_1_y4, n1_to_8_demultiplexer_1_y5,
       n1_to_8_demultiplexer_1_y6, n1_to_8_demultiplexer_1_y7;
  wire [7:0] main_1_out_5, main_2_out_5, main_3_out_5, main_4_out_5, main_5_out_5, main_6_out_5,
       main_7_out_5, main_8_out_5;

  Clock clock_1 (.out(clock_1_out));
  _1_to_8_Demultiplexer u_1_to_8_demultiplexer_1 (
    .D(clock_1_out), .Y7(n1_to_8_demultiplexer_1_y7), .Y6(n1_to_8_demultiplexer_1_y6),
    .Y5(n1_to_8_demultiplexer_1_y5), .Y4(n1_to_8_demultiplexer_1_y4), .Y3(n1_to_8_demultiplexer_1_y3),
    .Y2(n1_to_8_demultiplexer_1_y2), .Y1(n1_to_8_demultiplexer_1_y1), .Y0(n1_to_8_demultiplexer_1_y0),
    .S2(in_4[2]), .S1(in_4[1]), .S0(in_4[0]));
  REGISTRADOR_8BITS_main main_1 (
    .PRESET(SET), .CLK(n1_to_8_demultiplexer_1_y7), .CLEAR(CLEAR), .out_5(main_1_out_5), .in_4(in_1));
  REGISTRADOR_8BITS_main main_2 (
    .PRESET(SET), .CLK(n1_to_8_demultiplexer_1_y6), .CLEAR(CLEAR), .out_5(main_2_out_5), .in_4(in_1));
  REGISTRADOR_8BITS_main main_3 (
    .PRESET(SET), .CLK(n1_to_8_demultiplexer_1_y5), .CLEAR(CLEAR), .out_5(main_3_out_5), .in_4(in_1));
  REGISTRADOR_8BITS_main main_4 (
    .PRESET(SET), .CLK(n1_to_8_demultiplexer_1_y4), .CLEAR(CLEAR), .out_5(main_4_out_5), .in_4(in_1));
  REGISTRADOR_8BITS_main main_5 (
    .PRESET(SET), .CLK(n1_to_8_demultiplexer_1_y3), .CLEAR(CLEAR), .out_5(main_5_out_5), .in_4(in_1));
  REGISTRADOR_8BITS_main main_6 (
    .PRESET(SET), .CLK(n1_to_8_demultiplexer_1_y2), .CLEAR(CLEAR), .out_5(main_6_out_5), .in_4(in_1));
  REGISTRADOR_8BITS_main main_7 (
    .PRESET(SET), .CLK(n1_to_8_demultiplexer_1_y1), .CLEAR(CLEAR), .out_5(main_7_out_5), .in_4(in_1));
  REGISTRADOR_8BITS_main main_8 (
    .PRESET(SET), .CLK(n1_to_8_demultiplexer_1_y0), .CLEAR(CLEAR), .out_5(main_8_out_5), .in_4(in_1));
  MUX_8X1_8bits mux_8x1_8bits_1 (
    .in_1(main_8_out_5), .in_2(main_7_out_5), .in_3(main_6_out_5), .in_4(main_5_out_5), .in_5(in_5),
    .in_6(main_4_out_5), .in_7(main_3_out_5), .in_8(main_2_out_5), .in_9(main_1_out_5), .out_10(out_6));

  // Notes on the sheet:
  //   Y7
  //   Y6
  //   Y5
  //   Y4
  //   Y3
  //   Y2
  //   Y1
  //   Y0
endmodule
