// Logisim project REGISTRADOR 1bit.circ as structural Verilog: 1 circuit, main circuit main
module main (
  input  PRESET,
  input  D,
  input  CLK,
  input  CLEAR,
  output Q,
  output nQ
);

  wire nand_1_out, nand_2_out, nand_3_out, nand_4_out, nand_5_out, nand_6_out, not_1_out, not_2_out,
       not_3_out, not_4_out;

  not not_1 (not_1_out, D);
  not not_2 (not_2_out, PRESET);
  nand nand_1 (nand_1_out, nQ, D, CLK);
  not not_3 (not_3_out, CLK);
  nand nand_2 (nand_2_out, CLK, not_1_out, Q);
  not not_4 (not_4_out, CLEAR);
  nand nand_3 (nand_3_out, not_2_out, nand_1_out, nand_4_out);
  nand nand_4 (nand_4_out, nand_3_out, nand_2_out, not_4_out);
  nand nand_5 (nand_5_out, not_4_out, nand_3_out, not_3_out);
  nand nand_6 (nand_6_out, not_3_out, nand_4_out, not_2_out);
  nand nand_7 (Q, not_2_out, nand_5_out, nQ);
  nand nand_8 (nQ, Q, nand_6_out, not_4_out);
endmodule
