// Logisim project REGISTRADOR 8BITS.circ as structural Verilog: 1 circuit, main circuit main
module main (
  input  PRESET,
  input  CLK,
  input  CLEAR,
  input  [7:0] in_4,
  output [7:0] out_5
);

  REGISTRADOR_1bit_main main_1 (.PRESET(PRESET), .D(in_4[0]), .CLK(CLK), .CLEAR(CLEAR), .Q(out_5[0]));  // open: nQ
  REGISTRADOR_1bit_main main_2 (.PRESET(PRESET), .D(in_4[1]), .CLK(CLK), .CLEAR(CLEAR), .Q(out_5[1]));  // open: nQ
  REGISTRADOR_1bit_main main_3 (.PRESET(PRESET), .D(in_4[2]), .CLK(CLK), .CLEAR(CLEAR), .Q(out_5[2]));  // open: nQ
  REGISTRADOR_1bit_main main_4 (.PRESET(PRESET), .D(in_4[3]), .CLK(CLK), .CLEAR(CLEAR), .Q(out_5[3]));  // open: nQ
  REGISTRADOR_1bit_main main_5 (.PRESET(PRESET), .D(in_4[4]), .CLK(CLK), .CLEAR(CLEAR), .Q(out_5[4]));  // open: nQ
  REGISTRADOR_1bit_main main_6 (.PRESET(PRESET), .D(in_4[5]), .CLK(CLK), .CLEAR(CLEAR), .Q(out_5[5]));  // open: nQ
  REGISTRADOR_1bit_main main_7 (.PRESET(PRESET), .D(in_4[6]), .CLK(CLK), .CLEAR(CLEAR), .Q(out_5[6]));  // open: nQ
  REGISTRADOR_1bit_main main_8 (.PRESET(PRESET), .D(in_4[7]), .CLK(CLK), .CLEAR(CLEAR), .Q(out_5[7]));  // open: nQ
endmodule
