// Logisim project 8-somador de 8 bits.circ as structural Verilog: 5 circuits, main circuit Porta XOR
module Porta_XOR (
  input  A,
  input  B,
  output out_3
);

  wire and_1_out, and_2_out, not_1_out, not_2_out;

  not not_1 (not_1_out, B);
  not not_2 (not_2_out, A);
  and and_1 (and_1_out, not_1_out, A);
  and and_2 (and_2_out, B, not_2_out);
  or or_1 (out_3, and_1_out, and_2_out);

  // Notes on the sheet:
  //   S = (~A. B)+(A . ~B)
endmodule

module Meio_somador (
  input  a,
  input  b,
  output S,
  output Co
);

  Porta_XOR porta_xor_1 (.out_3(S), .A(b), .B(a));
  and and_1 (Co, a, b);
endmodule

module Somador_completo (
  input  Ci,
  input  a,
  input  b,
  output S,
  output Co
);

  wire meio_somador_1_co, meio_somador_1_s, meio_somador_2_co;

  Meio_somador meio_somador_1 (.a(a), .b(b), .S(meio_somador_1_s), .Co(meio_somador_1_co));
  Meio_somador meio_somador_2 (.a(Ci), .b(meio_somador_1_s), .S(S), .Co(meio_somador_2_co));
  or or_1 (Co, meio_somador_2_co, meio_somador_1_co);
endmodule

module somador_4_bits (
  input  Co,
  input  A0,
  input  B0,
  input  A1,
  input  B1,
  input  A2,
  input  B2,
  input  A3,
  input  B3,
  output S0,
  output S1,
  output S2,
  output S3,
  output C4
);

  wire somador_completo_1_co, somador_completo_2_co, somador_completo_3_co;

  Somador_completo somador_completo_1 (.Ci(Co), .a(A0), .b(B0), .S(S0), .Co(somador_completo_1_co));
  Somador_completo somador_completo_2 (.Ci(somador_completo_1_co), .a(A1), .b(B1), .S(S1), .Co(somador_completo_2_co));
  Somador_completo somador_completo_3 (.Ci(somador_completo_2_co), .a(A2), .b(B2), .S(S2), .Co(somador_completo_3_co));
  Somador_completo somador_completo_4 (.Ci(somador_completo_3_co), .a(A3), .b(B3), .S(S3), .Co(C4));
endmodule

module Somador_8_bits (
  input  Ci,
  input  A0,
  input  B0,
  input  A1,
  input  B1,
  input  A2,
  input  B2,
  input  A3,
  input  B3,
  input  A4,
  input  B4,
  input  A5,
  input  B5,
  input  A6,
  input  B6,
  input  A7,
  input  B7,
  output [7:0] out_18,
  output Overflow
);

  wire somador_4_bits_1_c4;

  somador_4_bits somador_4_bits_1 (
    .Co(Ci), .A0(A0), .B0(B0), .A1(A1), .B1(B1), .A2(A2), .B2(B2), .A3(A3), .B3(B3), .S0(out_18[0]),
    .S1(out_18[1]), .S2(out_18[2]), .S3(out_18[3]), .C4(somador_4_bits_1_c4));
  somador_4_bits somador_4_bits_2 (
    .Co(somador_4_bits_1_c4), .A0(A4), .B0(B4), .A1(A5), .B1(B5), .A2(A6), .B2(B6), .A3(A7), .B3(B7),
    .S0(out_18[4]), .S1(out_18[5]), .S2(out_18[6]), .S3(out_18[7]), .C4(Overflow));
endmodule
